# Fritzing sketch Garage Layout ESP32U Breadboard (saved by Fritzing 1.0.7)
perfboards: 1

parts:
  IC4 = IC, DIP package, 4 pins [chip_label=G3VM]
  A1 = Esp32-c3 super mini
  JP3 = Header 6 [package=1x06_smd_straight_alt]
  R4 = Resistor Mini [tolerance=±5% resistance=220 package=THT]

nets:
  N1: IC4.pin1, R4.Pin_1
  N2: IC4.pin2, A1.Pin_15, JP3.3
  N3: A1.Pin_13, R4.Pin_0
  N4: A1.Pin_16, JP3.1

notes:
  GPIO04

custom parts:
  Esp32-c3 super mini: ESP32-C3 Development Board ESP32 SuperMini Development Board ESP32 Development Board WiFi Bluetooth.
  Resistor Mini: A generic resistor (0.25W)
