# Fritzing sketch Garage Loyout 24x10 (saved by Fritzing 1.0.7)
perfboards: 1

parts:
  WeMos_D1_Mini1 = WeMos D1 Mini
  IC4 = IC, DIP package, 4 pins [chip_label=G3VM]
  IC5 = IC, DIP package, 4 pins [chip_label=G3VM]
  IC6 = IC, DIP package, 4 pins [chip_label=G3VM]
  IC7 = IC, DIP package, 4 pins [chip_label=G3VM]
  JP2 = Header 8 [package=1x08_smd]
  R2 = Resistor Mini [tolerance=±5% resistance=47000 package=THT]
  R3 = Resistor Mini [tolerance=±5% resistance=47000 package=THT]
  R4 = Resistor Mini [tolerance=±5% resistance=220 package=THT]
  R5 = Resistor Mini [tolerance=±5% resistance=220 package=THT]
  R6 = Resistor Mini [tolerance=±5% resistance=220 package=THT]
  R7 = Resistor Mini [tolerance=±5% resistance=220 package=THT]

nets:
  N1: WeMos_D1_Mini1.3V3, IC7.pin4
  N2: WeMos_D1_Mini1.D1, IC5.pin3, R2.Pin_1
  N3: WeMos_D1_Mini1.D2, IC7.pin3, R3.Pin_1
  N4: WeMos_D1_Mini1.D5, IC4.pin1
  N5: IC4.pin2, R4.Pin_1
  N6: IC4.pin3, JP2.2
  N7: IC4.pin4, JP2.1
  N8: IC5.pin1, R6.Pin_0
  N9: IC5.pin2, JP2.5
  N10: IC5.pin4, R2.Pin_0, R3.Pin_0, R4.Pin_0, R5.Pin_0
  N11: IC6.pin2, R5.Pin_1
  N12: IC6.pin3, JP2.4
  N13: IC6.pin4, JP2.3
  N14: IC7.pin2, JP2.7
  N15: JP2.6, R6.Pin_1
  N16: JP2.8, R7.Pin_1

custom parts:
  Resistor Mini: A generic resistor (0.25W)
