# Fritzing sketch Garage v2 Layout ESP32C3 size with I2C Pins 01 03 and 07 (saved by Fritzing 1.0.7)
perfboards: 1

parts:
  IC4 = IC, DIP package, 4 pins [chip_label=G3VM]
  R4 = Resistor Mini [tolerance=±5% resistance=220 package=THT]
  R5 = Resistor Mini [tolerance=±5% resistance=4700 package=THT]  # not connected
  JP4 = Header 1 [package=1x01_offset]
  JP5 = Header 1 [package=1x01_offset]  # not connected
  JP6 = Header 1 [package=1x01_offset]
  JP7 = Header 1 [package=1x01_offset]  # not connected
  JP8 = Header 1 [package=1x01_offset]  # not connected
  JP9 = Header 1 [package=1x01_offset]  # not connected
  R7 = Resistor Mini [tolerance=±5% resistance=4700 power=0W package=THT]  # not connected
  A1 = Esp32-c3 super mini

nets:
  N1: IC4.pin4, JP4.1
  N2: R4.Pin_1, A1.Pin_15
  N3: JP6.1, A1.Pin_14

custom parts:
  Resistor Mini: A generic resistor (0.25W)
  Esp32-c3 super mini: ESP32-C3 Development Board ESP32 SuperMini Development Board ESP32 Development Board WiFi Bluetooth.
