# Fritzing sketch Garage v2 Layout ESP32U with I2C side socket Protoboard 24x18 (saved by Fritzing 1.0.7)
perfboards: 1

parts:
  IC4 = IC, DIP package, 4 pins [chip_label=G3VM]
  JP3 = Header 6 [package=1x06_smd_straight_alt]
  R4 = Resistor Mini [tolerance=±5% resistance=220 package=THT]
  U1 = ESP32-38PinWide [part_number=ESP32-38PinWide]
  R5 = Resistor Mini [tolerance=±5% resistance=4700 package=THT]
  R6 = Resistor Mini [tolerance=±5% resistance=4700 package=THT]

nets:
  N1: IC4.pin1, R4.Pin_0
  N2: IC4.pin2, JP3.4, U1.GND
  N3: JP3.6, U1.VIN
  N4: U1.GPIO26, R6.Pin_1
  N5: U1.GPIO27, R5.Pin_1
  N6: U1.GPIO12, R5.Pin_0

custom parts:
  Resistor Mini: A generic resistor (0.25W)
  ESP32-38PinWide: Generic 38-Pin ESP32 with wide format (only access to one side of pins on a breadboard) based on Stephen Lilley's HiLetgo ESP-WROOM-32 ESP32 ESP-32S Development Board.
